# Fritzing sketch Untitled Sketch 2 (saved by Fritzing 0.9.3b)
breadboards: 1

parts:
  U2 = ESP32S-HiLetgo [part_number=ESP32S-HiLetgo]
  IC1 = Voltage Regulator [package=to-220-alt]
  R_Shunt = Resistor [tolerance=±5% resistance=1 package=THT]
  D2 = Schottky Diode [part_number=1N5817 package="300 mil [THT]"]
  U1 = L298 [package=multiwatt15]
  D1 = Schottky Diode [part_number=1N5817 package="300 mil [THT]"]
  M1 = DC Motor
  D3 = Schottky Diode [part_number=1N5817 package="300 mil [THT]"]
  J1_12V = Screw terminal - 2 pins [package=THT]
  D4 = Schottky Diode [part_number=1N5817 package="300 mil [THT]"]
  U4 = 74HC595 [package="DIP16 [THT]"]
  Sens1 = Screw terminal - 2 pins [package=THT]
  Sens2 = Screw terminal - 2 pins [package=THT]
  R2 = Resistor [tolerance=±5% resistance=10k package="0603 [SMD]"]
  R3 = Resistor [tolerance=±5% resistance=10k package="0603 [SMD]"]
  C2 = Electrolytic Capacitor [capacitance=100nF package="100 mil [THT, electrolytic]"]
  0_33uF = Electrolytic Capacitor [capacitance=1µF package="100 mil [THT, electrolytic]"]
  C3 = Electrolytic Capacitor [capacitance=100nF package="100 mil [THT, electrolytic]"]

nets:
  N1: U2.3.3, Sens1.pin1, Sens2.pin1
  N2: U2.GPIO26, R_Shunt.Pin_1, U1.CSA, U1.CSB
  N3: U2.GPIO27, U4.ST_CP
  N4: U2.GPIO14, U4.SH_CP
  GND: U2.GND, R_Shunt.Pin_0, D2.anode, U1.GND, J1_12V.pin1, D4.anode, U4.GND, U4.OE, R2.Pin_1, R3.Pin_1, C3.-
  N5: U2.GPIO13, U4.DS
  VIN: U2.VIN, IC1.OUT, U1.VLS, U4.MR, U4.VCC, C2.+
  N6: U2.GPIO0, Sens2.pin2, R3.Pin_0
  N7: U2.GPIO4, Sens1.pin2, R2.Pin_0
  N8: IC1.GND, C2.-, 0_33uF.-
  N9: IC1.IN, 0_33uF.+
  N10: D2.cathode, U1.OUT2, U1.OUT3, D1.anode, M1.pin_2
  N11: U1.OUT1, U1.OUT4, M1.pin_1, D3.anode, D4.cathode
  N12: U1.VS, D1.cathode, D3.cathode, J1_12V.pin2, C3.+
  N13: U1.IN1, U4.Q1
  N14: U1.ENA, U1.ENB, U4.Q5
  N15: U1.IN2, U4.Q2
  N16: U1.IN3, U4.Q3
  N17: U1.IN4, U4.Q4

custom parts:
  ESP32S-HiLetgo: HiLetgo ESP-WROOM-32 ESP32 ESP-32S Development Board 2.4GHz Dual-Mode WiFi + Bluetooth Dual Cores Microcontroller The ESP32 integrated with Antenna switches, RF Balun, power amplifiers, low-noise amplifiers, filters, and management modules, and the entire solution occupies the least area of PCB. 2.4 GHz Wi-Fi plus Bluetooth dual-mode chip, with TSMC Ultra-low power consumption 40nm technology,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
