# Fritzing sketch motor_driver (saved by Fritzing 0.9.3b)
circuit board: 5.33cm x 8.13cm
breadboards: 1

parts:
  U2 = ESP32S-HiLetgo [part_number=ESP32S-HiLetgo]
  D2 = Schottky Diode [part_number=1N5817 package="300 mil [THT]"]
  D1 = Schottky Diode [part_number=1N5817 package="300 mil [THT]"]
  D3 = Schottky Diode [part_number=1N5817 package="300 mil [THT]"]
  D4 = Schottky Diode [part_number=1N5817 package="300 mil [THT]"]
  C2 = Electrolytic Capacitor [capacitance=100nF package="100 mil [THT, electrolytic]"]
  0_33uF = Electrolytic Capacitor [capacitance=1µF package="100 mil [THT, electrolytic]"]
  C3 = Electrolytic Capacitor [capacitance=100nF package="100 mil [THT, electrolytic]"]
  IC2 = Voltage Regulator [package=to220-igo]
  J1 = female pin header, 1 pin [form="♀ (female)"]
  J2 = female pin header, 1 pin [form="♀ (female)"]
  R2 = Resistor [tolerance=±5% resistance=10k package=THT]
  R3 = Resistor [tolerance=±5% resistance=10k package=THT]
  SensUp = Screw terminal - 2 pins [package=THT]
  SensDown = Screw terminal - 2 pins [package=THT]
  J1_12V = Screw terminal - 2 pins [package=THT]
  Motor_Terminal = Screw terminal - 2 pins [package=THT]
  U1 = L298 [package=multiwatt15]
  U4 = 74HC595 [package="DIP16 [THT]"]

nets:
  N1: U2.3.3, SensUp.pin1, SensDown.pin1
  N2: U2.GPIO34, J1.pin1, U1.CSA, U1.CSB
  N3: U2.GPIO35, R3.Pin_0, SensUp.pin2
  N4: U2.GPIO32, R2.Pin_0, SensDown.pin2
  N5: U2.GPIO14, U4.SH_CP
  N6: U2.GPIO12, U4.ST_CP
  GND: U2.GND, D2.anode, D4.anode, C2.-, 0_33uF.-, C3.-, IC2.GND, J2.pin1, R2.Pin_1, R3.Pin_1, J1_12V.pin1, U1.GND, U4.GND, U4.OE
  N7: U2.GPIO13, U4.DS
  VIN: U2.VIN, C2.+, IC2.OUT, U1.VLS, U4.MR, U4.VCC
  N8: D2.cathode, D1.anode, Motor_Terminal.pin2, U1.OUT2, U1.OUT3
  N9: D1.cathode, D3.cathode, 0_33uF.+, C3.+, IC2.IN, J1_12V.pin2, U1.VS
  N10: D3.anode, D4.cathode, Motor_Terminal.pin1, U1.OUT1, U1.OUT4
  N11: U1.IN1, U1.IN4, U4.Q2
  N12: U1.ENA, U1.ENB, U4.Q0
  N13: U1.IN2, U1.IN3, U4.Q1

custom parts:
  ESP32S-HiLetgo: HiLetgo ESP-WROOM-32 ESP32 ESP-32S Development Board 2.4GHz Dual-Mode WiFi + Bluetooth Dual Cores Microcontroller The ESP32 integrated with Antenna switches, RF Balun, power amplifiers, low-noise amplifiers, filters, and management modules, and the entire solution occupies the least area of PCB. 2.4 GHz Wi-Fi plus Bluetooth dual-mode chip, with TSMC Ultra-low power consumption 40nm technology,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
